# Fritzing sketch headers (saved by Fritzing 0.8.5b)
circuit board: 10.1776cm x 5.36194cm
breadboards: 1

parts:
  Q6 = Basic FET P-Channel [package="TO220 [THT]"]
  Q1 = Basic FET P-Channel [package="TO220 [THT]"]
  Q5 = Basic FET P-Channel [package="TO220 [THT]"]
  Q2 = Basic FET P-Channel [package="TO220 [THT]"]
  Q3 = Basic FET P-Channel [package="TO220 [THT]"]
  Q4 = Basic FET P-Channel [package="TO220 [THT]"]
  Q7 = Basic FET P-Channel [package="TO220 [THT]"]
  Q8 = Basic FET P-Channel [package="TO220 [THT]"]
  Q9 = Basic FET P-Channel [package="TO220 [THT]"]
  Q10 = Basic FET P-Channel [package="TO220 [THT]"]
  Q11 = Basic FET P-Channel [package="TO220 [THT]"]
  Q12 = Basic FET P-Channel [package="TO220 [THT]"]
  Q13 = Basic FET P-Channel [package="TO220 [THT]"]
  Q14 = Basic FET P-Channel [package="TO220 [THT]"]
  J1 = Infrared Proximity Sensor
  J2 = Infrared Proximity Sensor
  J3 = Infrared Proximity Sensor
  J4 = Infrared Proximity Sensor
  J5 = Infrared Proximity Sensor
  Q15 = Basic FET P-Channel [package="TO220 [THT]"]
  JP1 = Header 2 [package=screwterminal-3.5mm-2_lock]
  JP2 = Header 2 [package=screwterminal-3.5mm-2_lock]
  Part1 = Arduino Mega 2560 (Rev3)
  J6 = screw terminal, 2 pins  # not connected
  J6_2 = screw terminal, 2 pins  # not connected
  J6_3 = screw terminal, 2 pins  # not connected

nets:
  N1: Q6.gate, Part1.D5_PWM
  GND: Q6.source, Q1.source, Q5.source, Q2.source, Q3.source, Q4.source, Q7.source, Q8.source, Q9.source, Q10.source, Q11.source, Q12.source, Q13.source, Q14.source, J1.GND, J2.GND, J3.GND, J4.GND, J5.GND, Q15.source, Part1.GND
  N2: Q1.gate, Part1.D45
  N3: Q1.drain, JP1.2
  N4: Q5.gate, Part1.D4_PWM
  N5: Q2.gate, Part1.D44
  N6: Q3.gate, Part1.D2_PWM
  N7: Q3.drain, JP2.1
  N8: Q4.gate, Part1.D3_PWM
  N9: Q7.gate, Part1.D6_PWM
  N10: Q8.gate, Part1.D7_PWM
  N11: Q9.gate, Part1.D8_PWM
  N12: Q10.gate, Part1.D9_PWM
  N13: Q11.gate, Part1.D10_PWM
  N14: Q12.gate, Part1.D11_PWM
  N15: Q13.gate, Part1.D12_PWM
  N16: Q14.gate, Part1.D13_PWM
  N17: J1.Vout, Part1.A1
  VCC: J1.Vcc, J2.Vcc, J3.Vcc, J4.Vcc, J5.Vcc, Part1.5V
  N18: J2.Vout, Part1.A0
  N19: J3.Vout, Part1.A2
  N20: J4.Vout, Part1.A3
  N21: J5.Vout, Part1.A4
  N22: Q15.gate, Part1.D46
  N23: JP1.1, JP2.2, Part1.VIN
