# Fritzing sketch lightwall schematic (saved by Fritzing 0.8.5b)
circuit board: 8.46667cm x 5.64444cm
breadboards: 1

parts:
  Q6 = Basic FET P-Channel [package="TO220 [THT]"]
  Part1 = Arduino Mega 2560 (Rev3)
  Q1 = Basic FET P-Channel [package="TO220 [THT]"]
  Q5 = Basic FET P-Channel [package="TO220 [THT]"]
  Q2 = Basic FET P-Channel [package="TO220 [THT]"]
  Q3 = Basic FET P-Channel [package="TO220 [THT]"]
  Q4 = Basic FET P-Channel [package="TO220 [THT]"]
  Q7 = Basic FET P-Channel [package="TO220 [THT]"]
  Q8 = Basic FET P-Channel [package="TO220 [THT]"]
  Q9 = Basic FET P-Channel [package="TO220 [THT]"]
  Q10 = Basic FET P-Channel [package="TO220 [THT]"]
  Q11 = Basic FET P-Channel [package="TO220 [THT]"]
  Q12 = Basic FET P-Channel [package="TO220 [THT]"]
  Q13 = Basic FET P-Channel [package="TO220 [THT]"]
  Q14 = Basic FET P-Channel [package="TO220 [THT]"]
  J1 = Infrared Proximity Sensor
  J2 = Infrared Proximity Sensor
  NEOPIXEL1 = Neopixel Strip -- White (60/m)
  NEOPIXEL2 = Neopixel Strip -- White (60/m)
  NEOPIXEL3 = Neopixel Strip -- White (60/m)
  NEOPIXEL4 = Neopixel Strip -- White (60/m)
  NEOPIXEL5 = Neopixel Strip -- White (60/m)
  NEOPIXEL6 = Neopixel Strip -- White (60/m)
  NEOPIXEL7 = Neopixel Strip -- White (60/m)
  NEOPIXEL8 = Neopixel Strip -- White (60/m)
  NEOPIXEL9 = Neopixel Strip -- White (60/m)
  NEOPIXEL10 = Neopixel Strip -- White (60/m)
  NEOPIXEL11 = Neopixel Strip -- White (60/m)
  NEOPIXEL12 = Neopixel Strip -- White (60/m)
  NEOPIXEL13 = Neopixel Strip -- White (60/m)
  NEOPIXEL14 = Neopixel Strip -- White (60/m)
  J3 = Infrared Proximity Sensor
  J4 = Infrared Proximity Sensor
  J5 = Infrared Proximity Sensor
  NEOPIXEL15 = Neopixel Strip -- White (60/m)
  Q15 = Basic FET P-Channel [package="TO220 [THT]"]

nets:
  N1: Q6.gate, Part1.D5_PWM
  N2: Q6.drain, NEOPIXEL6.GND
  GND: Q6.source, Part1.GND, Q1.source, Q5.source, Q2.source, Q3.source, Q4.source, Q7.source, Q8.source, Q9.source, Q10.source, Q11.source, Q12.source, Q13.source, Q14.source, J1.GND, J2.GND, J3.GND, J4.GND, J5.GND, Q15.source
  N3: Part1.A0, J2.Vout
  N4: Part1.A1, J1.Vout
  N5: Part1.A2, J3.Vout
  N6: Part1.A3, J4.Vout
  N7: Part1.A4, J5.Vout
  N8: Part1.D13_PWM, Q14.gate
  N9: Part1.D12_PWM, Q13.gate
  N10: Part1.D11_PWM, Q12.gate
  N11: Part1.D10_PWM, Q11.gate
  N12: Part1.D9_PWM, Q10.gate
  N13: Part1.D8_PWM, Q9.gate
  VCC: Part1.5V, J1.Vcc, J2.Vcc, J3.Vcc, J4.Vcc, J5.Vcc
  N14: Part1.VIN, NEOPIXEL1.DI, NEOPIXEL2.DI, NEOPIXEL3.DI, NEOPIXEL4.DI, NEOPIXEL5.DI, NEOPIXEL6.DI, NEOPIXEL7.DI, NEOPIXEL8.DI, NEOPIXEL9.DI, NEOPIXEL10.DI, NEOPIXEL11.DI, NEOPIXEL12.DI, NEOPIXEL13.DI, NEOPIXEL14.DI
  N15: Part1.D2_PWM, Q3.gate
  N16: Part1.D3_PWM, Q4.gate
  N17: Part1.D4_PWM, Q5.gate
  N18: Part1.D6_PWM, Q7.gate
  N19: Part1.D7_PWM, Q8.gate
  N20: Part1.D44, Q2.gate
  N21: Part1.D45, Q1.gate
  N22: Part1.D46, Q15.gate
  N23: Q1.drain, NEOPIXEL1.GND
  N24: Q5.drain, NEOPIXEL5.GND
  N25: Q2.drain, NEOPIXEL2.GND
  N26: Q3.drain, NEOPIXEL3.GND
  N27: Q4.drain, NEOPIXEL4.GND
  N28: Q7.drain, NEOPIXEL7.GND
  N29: Q8.drain, NEOPIXEL8.GND
  N30: Q9.drain, NEOPIXEL9.GND
  N31: Q10.drain, NEOPIXEL10.GND
  N32: Q11.drain, NEOPIXEL11.GND
  N33: Q12.drain, NEOPIXEL12.GND
  N34: Q13.drain, NEOPIXEL13.GND
  N35: Q14.drain, NEOPIXEL14.GND
  N36: NEOPIXEL15.GND, Q15.drain

custom parts:
  Neopixel Strip -- White (60/m): Neopixel Strip, White, 60 pixels per meter.
